# Fritzing sketch TFT_SerialLogger (saved by Fritzing 0.9.2b)

parts:
  U1 = IC, SIP package, 18 pins [chip_label="2.4\" TFT"]
  U2 = IC, SIP package, 6 pins [chip_label=Digitiser]
  U3 = IC, SIP package, 6 pins [chip_label=SD]
  Part1 = Arduino Nano (Rev3.0)
  BAT1 = BC9VPC [package=bc9vpc]
  U4 = SIP - 2 pins [chip_label=IC package="SIP (Single Inline) [THT]"]
  S1 = SPST Switch [package=switch-spdt]

nets:
  N1: U1.pin2, Part1.A3
  N2: U1.pin4, Part1.A2
  N3: U1.pin5, Part1.D7
  N4: U1.pin6, Part1.D6
  N5: U1.pin7, Part1.D5
  N6: U1.pin8, Part1.D4
  N7: U1.pin9, Part1.D3
  N8: U1.pin10, Part1.D2
  N9: U1.pin11, Part1.D1/TX
  N10: U1.pin12, Part1.D0/RX
  N11: U1.pin14, Part1.A4
  N12: U1.pin15, Part1.A5
  N13: U1.pin17, Part1.5V
  N14: U1.pin18, Part1.GND, BAT1.V-, U4.pin1
  N15: U2.pin6, Part1.D8
  N16: U3.pin1, Part1.D10
  N17: U3.pin2, Part1.D11/MOSI
  N18: U3.pin3, Part1.D13/SCK
  N19: U3.pin4, Part1.D12/MISO
  N20: Part1.D9, U4.pin2
  N21: Part1.VIN, S1.P
  N22: BAT1.V+, S1.O
